// Logisim project alu design 332.circ as structural Verilog: 6 circuits, main circuit R-TYPE
module R_TYPE (
  input  in_1,
  input  [3:0] in_2,
  input  [3:0] in_3,
  input  [3:0] in_4,
  input  [21:0] in_5,
  input  in_6,
  input  in_7,
  input  in_8,
  input  in_9,
  input  [2:0] in_10,
  input  in_11,
  output out_12,
  output out_13
);

  wire clock_1_out, clock_2_out;
  wire [21:0] adder_1_out, n22_bit_alu_1_out_6, register_1_q, rom_1_data, undriven, undriven_2;

  Register #(.width(22)) register_1 (.D(adder_1_out), .Q(register_1_q), .clk(clock_1_out), .clr(in_6));  // open: en
  Clock clock_1 (.out(clock_1_out));
  Adder #(.width(22)) adder_1 (.a(register_1_q), .b(22'h1), .out(adder_1_out), .cin(1'b0));  // open: cout
  ROM #(.addrWidth(22), .dataWidth(22)) rom_1 (.addr(register_1_q), .data(rom_1_data));  // open: sel
  _22_bit_alu u_22_bit_alu_1 (
    .B(undriven_2), .A(undriven), .in_4(rom_1_data[4:2]), .out_8(out_12), .in_5(in_10), .cout(out_13),
    .out_6(n22_bit_alu_1_out_6), .in_1(in_1));
  Clock clock_2 (.out(clock_2_out));

  // Notes on the sheet:
  //   contents of rom_1 (hex, n*v repeats v):
  //   697
endmodule

module _22_bit_alu (
  input  in_1,
  input  [21:0] B,
  input  [21:0] A,
  input  [2:0] in_4,
  input  [2:0] in_5,
  output [21:0] out_6,
  output cout,
  output out_8
);

  wire comparator_1_lt;
  wire [4:0] bit_extender_1_out;
  wire [21:0] adder_1_out, bit_extender_2_out, multiplexer_1_out, not_1_out, or_1_out, shifter_1_out,
       xor_1_out;

  assign not_1_out = ~B;  // NOT_Gate not_1, 22 bits wide
  Multiplexer #(.width(22)) multiplexer_1 (
    .in0(B), .in1(not_1_out), .out(multiplexer_1_out), .sel(in_5[0]));  // open: en
  assign bit_extender_1_out = {{2{1'b0}}, in_4};  // Bit_Extender bit_extender_1
  Adder #(.width(22)) adder_1 (.a(A), .b(multiplexer_1_out), .out(adder_1_out), .cin(in_1), .cout(cout));
  assign xor_1_out = A ^ B;  // XOR_Gate xor_1, 22 bits wide
  Shifter #(.width(22), .shift("lr")) shifter_1 (.in(A), .\dist (bit_extender_1_out), .out(shifter_1_out));
  assign or_1_out = A | B;  // OR_Gate or_1, 22 bits wide
  Comparator #(.width(22)) comparator_1 (.a(A), .b(B), .lt(comparator_1_lt));  // open: gt, eq
  assign bit_extender_2_out = {{21{1'b0}}, comparator_1_lt};  // Bit_Extender bit_extender_2
  Multiplexer #(.select(3), .width(22)) multiplexer_2 (
    .in0(adder_1_out), .in1(adder_1_out), .in2(xor_1_out), .in3(or_1_out), .in4(bit_extender_2_out),
    .in6(shifter_1_out), .out(out_6), .sel(in_5));  // open: in5, in7, en
  nor nor_1 (out_8, out_6[0], out_6[1], out_6[2], out_6[3], out_6[4], out_6[5], out_6[6], out_6[7], out_6[8], out_6[9], out_6[10], out_6[11], out_6[12], out_6[13], out_6[14], out_6[15], out_6[16], out_6[17], out_6[18], out_6[19], out_6[20], out_6[21]);

  // Notes on the sheet:
  //   FIG:  22 BIT ALU
  //   XOR
  //   SRL
  //   OR
  //   ADD
  //   SUB
endmodule

module COMPLETE_DATA_PATH (
  input  in_1,
  input  in_2,
  output out_3
);

  wire alu_control_unit_1_cin, clock_1_out, control_unit_1_alu_src, control_unit_1_branch, control_unit_1_lw,
       control_unit_1_memtoreg, control_unit_1_r_type, control_unit_1_regdest, control_unit_1_sw,
       control_unit_1_wc, n22_bit_alu_1_out_8, not_1_out;
  wire [1:0] and_1_out, control_unit_1_alu_op;
  wire [2:0] alu_control_unit_1_out_4;
  wire [3:0] multiplexer_2_out;
  wire [4:0] rom_1_data_2;
  wire [16:0] rom_1_data;
  wire [21:0] adder_1_out, adder_2_out, bit_extender_1_out, bit_extender_2_out, multiplexer_1_out,
       multiplexer_3_out, n22_bit_alu_1_out_6, PC_q, ram_1_data, register_file_1_p4, register_file_1_p8,
       register_file_1_p9;

  Multiplexer #(.select(2), .width(22)) multiplexer_1 (
    .in0(adder_1_out), .in1(adder_2_out), .in2(bit_extender_1_out), .out(multiplexer_1_out), .sel(and_1_out));  // open: in3, en
  Control_Unit control_unit_1 (
    .OPCODE(rom_1_data_2), .SW(control_unit_1_sw), .WC(control_unit_1_wc), .JUMP(and_1_out[1]),
    .RegDest(control_unit_1_regdest), .ALU_SRC(control_unit_1_alu_src), .BRANCH(control_unit_1_branch),
    .LW(control_unit_1_lw), .MemToReg(control_unit_1_memtoreg), .ALU_OP(control_unit_1_alu_op),
    .R_Type(control_unit_1_r_type));
  Register #(.width(22)) PC (.D(multiplexer_1_out), .Q(PC_q), .clk(clock_1_out), .clr(in_1));  // open: en
  Clock clock_1 (.out(clock_1_out));
  Adder #(.width(22)) adder_1 (.a(PC_q), .b(22'h1), .out(adder_1_out), .cin(1'b0));  // open: cout
  assign bit_extender_1_out = {{5{1'b0}}, rom_1_data};  // Bit_Extender bit_extender_1
  ROM #(.addrWidth(22), .dataWidth(22)) rom_1 (.addr(PC_q), .data({rom_1_data_2, rom_1_data}));  // open: sel
  Adder #(.width(22)) adder_2 (.a(adder_1_out), .b(bit_extender_2_out), .out(adder_2_out));  // open: cin, cout
  Multiplexer #(.width(4)) multiplexer_2 (
    .in0(rom_1_data[8:5]), .in1(rom_1_data[12:9]), .out(multiplexer_2_out), .sel(control_unit_1_regdest));  // open: en
  assign bit_extender_2_out = {{13{1'b0}}, rom_1_data[8:0]};  // Bit_Extender bit_extender_2
  // register_file register_file_1: pin names not known; wires that end beside it: rom_1_data[16:13], rom_1_data[12:9], multiplexer_2_out, register_file_1_p4, control_unit_1_wc, clock_1_out, in_2, register_file_1_p8, register_file_1_p9
  Multiplexer #(.width(22)) multiplexer_3 (
    .in0(register_file_1_p9), .in1(bit_extender_2_out), .out(multiplexer_3_out), .sel(control_unit_1_alu_src));  // open: en
  and and_1 (and_1_out[0], control_unit_1_branch, not_1_out);
  not not_1 (not_1_out, n22_bit_alu_1_out_8);
  _22_bit_alu u_22_bit_alu_1 (
    .B(multiplexer_3_out), .A(register_file_1_p8), .in_4(rom_1_data[4:2]), .out_8(n22_bit_alu_1_out_8),
    .in_5(alu_control_unit_1_out_4), .cout(out_3), .out_6(n22_bit_alu_1_out_6), .in_1(alu_control_unit_1_cin));
  alu_control_unit alu_control_unit_1 (
    .ALUOP(control_unit_1_alu_op), .FUNCTION(rom_1_data[1:0]), .in_3(control_unit_1_r_type),
    .out_4(alu_control_unit_1_out_4), .CIN(alu_control_unit_1_cin));
  RAM #(.addrWidth(22), .dataWidth(22), .bus("separate")) ram_1 (
    .addr(n22_bit_alu_1_out_6), .din(register_file_1_p9), .data(ram_1_data), .str(control_unit_1_sw),
    .clk(clock_1_out), .ld(control_unit_1_lw));  // open: sel, clr
  Multiplexer #(.width(22)) multiplexer_4 (
    .in0(n22_bit_alu_1_out_6), .in1(ram_1_data), .out(register_file_1_p4), .sel(control_unit_1_memtoreg));  // open: en

  // Notes on the sheet:
  //   INSTRUCTION MEMORY
  //   contents of rom_1 (hex, n*v repeats v):
  //   a0205 60004 a2201 a2201 a220a
  //   FUNCTION
  //   RD
  //   SHIFT
  //   RS
  //   RT
  //   IMMEDIATE
  //   FIG: COMPLETE DATAPATH
  //   BNE
  //   BRANCH
  //   ZERO FLAG
endmodule

module Control_Unit (
  input  [4:0] OPCODE,
  output SW,
  output WC,
  output JUMP,
  output RegDest,
  output ALU_SRC,
  output BRANCH,
  output LW,
  output MemToReg,
  output [1:0] ALU_OP,
  output R_Type
);

  wire decoder_1_out2, decoder_1_out5;

  Decoder #(.select(5)) decoder_1 (
    .out0(R_Type), .out1(BRANCH), .out2(decoder_1_out2), .out3(JUMP), .out4(SW), .out5(decoder_1_out5),
    .out6(LW), .sel(OPCODE));  // open: out7, out8, out9, out10, out11, out12, out13, out14, out15, out16, out17, out18, out19, out20, out21, out22, out23, out24, out25, out26, out27, out28, out29, out30, out31, en
  or or_1 (RegDest, decoder_1_out2, decoder_1_out5, LW);
  or or_2 (ALU_OP[1], decoder_1_out2, decoder_1_out5);
  or or_3 (WC, R_Type, decoder_1_out2, decoder_1_out5, LW);
  or or_4 (ALU_SRC, decoder_1_out2, SW, decoder_1_out5, LW);
  or or_5 (ALU_OP[0], BRANCH, decoder_1_out2);

  assign MemToReg = LW;

  // Notes on the sheet:
  //   FIG: CONTROL UNIT
  //   MSB
  //   LSB
endmodule

module PRAC (
);

  wire undriven;

  Demultiplexer demultiplexer_1 (.sel(undriven));  // open: out0, out1, in, en
endmodule

module alu_control_unit (
  input  [1:0] ALUOP,
  input  [1:0] FUNCTION,
  input  in_3,
  output [2:0] out_4,
  output CIN
);

  wire and_1_out, and_2_out, and_3_out, and_4_out, decoder_1_out0, decoder_1_out2, not_1_out, not_2_out;
  wire [1:0] multiplexer_1_out;

  Multiplexer #(.width(2)) multiplexer_1 (
    .in0(ALUOP), .in1(FUNCTION), .out(multiplexer_1_out), .sel(in_3));  // open: en
  Decoder #(.select(2)) decoder_1 (
    .out0(decoder_1_out0), .out1(CIN), .out2(decoder_1_out2), .out3(out_4[2]), .sel(multiplexer_1_out));  // open: en
  not not_1 (not_1_out, ALUOP[0]);
  and and_1 (and_1_out, not_1_out, ALUOP[1]);
  and and_2 (and_2_out, and_1_out, decoder_1_out2);
  not not_2 (not_2_out, ALUOP[1]);
  and and_3 (and_3_out, not_1_out, not_2_out);
  and and_4 (and_4_out, and_3_out, out_4[2]);
  or or_1 (out_4[0], and_2_out, CIN);
  or or_2 (out_4[1], and_4_out, decoder_1_out2);

  // Notes on the sheet:
  //   FIG: ALU CONTROL UNIT
endmodule
