// Logisim project register file 332 (1).circ as structural Verilog: 2 circuits, main circuit main
module main (
  input  [3:0] in_1,
  input  [3:0] in_2,
  input  [3:0] in_3,
  input  [21:0] in_4,
  input  in_5,
  input  in_6,
  output [21:0] out_7,
  output [21:0] out_8
);

  wire clock_1_out;

  register_file register_file_1 (
    .CLOCK(clock_1_out), .WC(in_6), .WRITE_DATA(in_4), .write_data_1(out_7), .CLEAR(in_5),
    .write_data_2(out_8), .WRITE_REGISTER(in_3), .rs(in_1), .rt(in_2));
  Clock clock_1 (.out(clock_1_out));
endmodule

module register_file (
  input  CLOCK,
  input  [3:0] rt,
  input  WC,
  input  [3:0] rs,
  input  CLEAR,
  input  [3:0] WRITE_REGISTER,
  input  [21:0] WRITE_DATA,
  output [21:0] write_data_1,
  output [21:0] write_data_2
);

  wire and_1_out, and_2_out, and_3_out, and_4_out, and_5_out, and_6_out, and_7_out, and_8_out, and_9_out,
       and_10_out, and_11_out, and_12_out, and_13_out, and_14_out, and_15_out, and_16_out, decoder_1_out0,
       decoder_1_out1, decoder_1_out2, decoder_1_out3, decoder_1_out4, decoder_1_out5, decoder_1_out6,
       decoder_1_out7, decoder_1_out8, decoder_1_out9, decoder_1_out10, decoder_1_out11, decoder_1_out12,
       decoder_1_out13, decoder_1_out14, decoder_1_out15;
  wire [21:0] REGISTER_00_q, REGISTER_01_q, REGISTER_02_q, REGISTER_03_q, REGISTER_04_q, REGISTER_05_q,
       REGISTER_06_q, REGISTER_07_q, REGISTER_08_q, REGISTER_09_q, REGISTER_10_prime_q, REGISTER_11_q,
       REGISTER_12_q, REGISTER_13_q, REGISTER_14_q, REGISTER_15_q;

  Decoder #(.select(4)) decoder_1 (
    .out0(decoder_1_out0), .out1(decoder_1_out1), .out2(decoder_1_out2), .out3(decoder_1_out3),
    .out4(decoder_1_out4), .out5(decoder_1_out5), .out6(decoder_1_out6), .out7(decoder_1_out7),
    .out8(decoder_1_out8), .out9(decoder_1_out9), .out10(decoder_1_out10), .out11(decoder_1_out11),
    .out12(decoder_1_out12), .out13(decoder_1_out13), .out14(decoder_1_out14), .out15(decoder_1_out15),
    .sel(WRITE_REGISTER));  // open: en
  and and_1 (and_1_out, decoder_1_out0, WC);
  and and_2 (and_2_out, decoder_1_out1, WC);
  and and_3 (and_3_out, decoder_1_out2, WC);
  and and_4 (and_4_out, decoder_1_out3, WC);
  and and_5 (and_5_out, decoder_1_out4, WC);
  and and_6 (and_6_out, decoder_1_out5, WC);
  and and_7 (and_7_out, decoder_1_out6, WC);
  and and_8 (and_8_out, decoder_1_out7, WC);
  Register #(.width(22)) REGISTER_00 (.D(WRITE_DATA), .en(and_1_out), .Q(REGISTER_00_q), .clk(CLOCK), .clr(CLEAR));
  Register #(.width(22)) REGISTER_01 (.D(WRITE_DATA), .en(and_2_out), .Q(REGISTER_01_q), .clk(CLOCK), .clr(CLEAR));
  Register #(.width(22)) REGISTER_02 (.D(WRITE_DATA), .en(and_3_out), .Q(REGISTER_02_q), .clk(CLOCK), .clr(CLEAR));
  Register #(.width(22)) REGISTER_03 (.D(WRITE_DATA), .en(and_4_out), .Q(REGISTER_03_q), .clk(CLOCK), .clr(CLEAR));
  Register #(.width(22)) REGISTER_04 (.D(WRITE_DATA), .en(and_5_out), .Q(REGISTER_04_q), .clk(CLOCK), .clr(CLEAR));
  Register #(.width(22)) REGISTER_05 (.D(WRITE_DATA), .en(and_6_out), .Q(REGISTER_05_q), .clk(CLOCK), .clr(CLEAR));
  Register #(.width(22)) REGISTER_06 (.D(WRITE_DATA), .en(and_7_out), .Q(REGISTER_06_q), .clk(CLOCK), .clr(CLEAR));
  Register #(.width(22)) REGISTER_07 (.D(WRITE_DATA), .en(and_8_out), .Q(REGISTER_07_q), .clk(CLOCK), .clr(CLEAR));
  and and_9 (and_9_out, decoder_1_out8, WC);
  and and_10 (and_10_out, decoder_1_out9, WC);
  and and_11 (and_11_out, decoder_1_out10, WC);
  and and_12 (and_12_out, decoder_1_out11, WC);
  and and_13 (and_13_out, decoder_1_out12, WC);
  and and_14 (and_14_out, decoder_1_out13, WC);
  and and_15 (and_15_out, decoder_1_out14, WC);
  and and_16 (and_16_out, decoder_1_out15, WC);
  Multiplexer #(.select(4), .width(22)) multiplexer_1 (
    .in0(REGISTER_00_q), .in1(REGISTER_01_q), .in2(REGISTER_02_q), .in3(REGISTER_03_q), .in4(REGISTER_04_q),
    .in5(REGISTER_05_q), .in6(REGISTER_06_q), .in7(REGISTER_07_q), .in8(REGISTER_08_q), .in9(REGISTER_09_q),
    .in10(REGISTER_10_prime_q), .in11(REGISTER_11_q), .in12(REGISTER_12_q), .in13(REGISTER_13_q),
    .in14(REGISTER_14_q), .in15(REGISTER_15_q), .out(write_data_1), .sel(rs));  // open: en
  Register #(.width(22)) REGISTER_08 (.D(WRITE_DATA), .en(and_9_out), .Q(REGISTER_08_q), .clk(CLOCK), .clr(CLEAR));
  Register #(.width(22)) REGISTER_09 (.D(WRITE_DATA), .en(and_10_out), .Q(REGISTER_09_q), .clk(CLOCK), .clr(CLEAR));
  Register #(.width(22)) REGISTER_10_prime (
    .D(WRITE_DATA), .en(and_11_out), .Q(REGISTER_10_prime_q), .clk(CLOCK), .clr(CLEAR));
  Register #(.width(22)) REGISTER_11 (.D(WRITE_DATA), .en(and_12_out), .Q(REGISTER_11_q), .clk(CLOCK), .clr(CLEAR));
  Register #(.width(22)) REGISTER_12 (.D(WRITE_DATA), .en(and_13_out), .Q(REGISTER_12_q), .clk(CLOCK), .clr(CLEAR));
  Register #(.width(22)) REGISTER_13 (.D(WRITE_DATA), .en(and_14_out), .Q(REGISTER_13_q), .clk(CLOCK), .clr(CLEAR));
  Register #(.width(22)) REGISTER_14 (.D(WRITE_DATA), .en(and_15_out), .Q(REGISTER_14_q), .clk(CLOCK), .clr(CLEAR));
  Register #(.width(22)) REGISTER_15 (.D(WRITE_DATA), .en(and_16_out), .Q(REGISTER_15_q), .clk(CLOCK), .clr(CLEAR));
  Multiplexer #(.select(4), .width(22)) multiplexer_2 (
    .in0(REGISTER_00_q), .in1(REGISTER_01_q), .in2(REGISTER_02_q), .in3(REGISTER_03_q), .in4(REGISTER_04_q),
    .in5(REGISTER_05_q), .in6(REGISTER_06_q), .in7(REGISTER_07_q), .in8(REGISTER_08_q), .in9(REGISTER_09_q),
    .in10(REGISTER_10_prime_q), .in11(REGISTER_11_q), .in12(REGISTER_12_q), .in13(REGISTER_13_q),
    .in14(REGISTER_14_q), .in15(REGISTER_15_q), .out(write_data_2), .sel(rt));  // open: en
endmodule
